// Logisim project hey.circ as structural Verilog: 16 circuits, main circuit main
module main (
  input  S,
  input  I,
  input  A0,
  input  A1,
  input  E,
  output out_6,
  output out_7
);

  wire mux_2_1_1_out_4, mux_2_1_2_out_4;

  MUX_2_1 mux_2_1_1 (.I0(A0), .I1(I), .S0(S), .out_4(mux_2_1_1_out_4));
  D_LATCH d_latch_1 (.D(mux_2_1_1_out_4), .E(E), .Q(out_6));
  MUX_2_1 mux_2_1_2 (.I0(A1), .I1(A0), .S0(S), .out_4(mux_2_1_2_out_4));
  D_LATCH d_latch_2 (.D(mux_2_1_2_out_4), .E(E), .Q(out_7));
endmodule

module XOR_GATE (
  input  in_1,
  input  in_2,
  output out_3
);

  wire and_1_out, and_2_out, not_1_out, not_2_out;

  not not_1 (not_1_out, in_2);
  not not_2 (not_2_out, in_1);
  and and_1 (and_1_out, in_1, not_1_out);
  and and_2 (and_2_out, not_2_out, in_2);
  or or_1 (out_3, and_1_out, and_2_out);
endmodule

module half_adder (
  input  A,
  input  B,
  output Sum,
  output Carry
);

  and and_1 (Carry, A, B);
  XOR_GATE xor_gate_1 (.in_1(A), .in_2(B), .out_3(Sum));
endmodule

module FULL_ADDER (
  input  A,
  input  B,
  input  C,
  output Sum,
  output Carry
);

  wire half_adder_1_carry, half_adder_1_sum, half_adder_2_carry;

  half_adder half_adder_1 (.A(A), .B(B), .Sum(half_adder_1_sum), .Carry(half_adder_1_carry));
  half_adder half_adder_2 (.A(half_adder_1_sum), .B(C), .Sum(Sum), .Carry(half_adder_2_carry));
  or or_1 (Carry, half_adder_2_carry, half_adder_1_carry);
endmodule

module FourB_ADDER (
  input  Y3,
  input  X3,
  input  Y2,
  input  X2,
  input  Y1,
  input  X1,
  input  Y0,
  input  X0,
  input  C,
  output Carry,
  output S3,
  output S2,
  output S1,
  output S0
);

  wire full_adder_2_carry, full_adder_3_carry, full_adder_4_carry;

  FULL_ADDER full_adder_1 (.A(X3), .B(Y3), .C(full_adder_2_carry), .Sum(S3), .Carry(Carry));
  FULL_ADDER full_adder_2 (.A(X2), .B(Y2), .C(full_adder_3_carry), .Sum(S2), .Carry(full_adder_2_carry));
  FULL_ADDER full_adder_3 (.A(X1), .B(Y1), .C(full_adder_4_carry), .Sum(S1), .Carry(full_adder_3_carry));
  FULL_ADDER full_adder_4 (.A(X0), .B(Y0), .C(C), .Sum(S0), .Carry(full_adder_4_carry));
endmodule

module ADDSUB4BIT (
  input  X3,
  input  X2,
  input  X1,
  input  X0,
  input  Y3,
  input  Y2,
  input  Y1,
  input  Y0,
  input  SUB,
  output Carry,
  output S3,
  output S2,
  output S1,
  output S0
);

  wire xor_1_out, xor_2_out, xor_3_out, xor_4_out;

  xor xor_1 (xor_1_out, Y3, SUB);
  xor xor_2 (xor_2_out, Y2, SUB);
  xor xor_3 (xor_3_out, Y1, SUB);
  xor xor_4 (xor_4_out, Y0, SUB);
  FourB_ADDER fourb_adder_1 (
    .Y3(xor_1_out), .X3(X3), .Y2(xor_2_out), .X2(X2), .Y1(xor_3_out), .X1(X1), .Y0(xor_4_out), .X0(X0),
    .C(SUB), .Carry(Carry), .S3(S3), .S2(S2), .S1(S1), .S0(S0));
endmodule

module BCD_Detector (
  input  A3,
  input  A2,
  input  A1,
  input  A0,
  output out_5
);

  wire and_1_out, and_2_out, not_1_out, not_2_out, not_3_out;

  not not_1 (not_1_out, A2);
  not not_2 (not_2_out, A1);
  and and_1 (and_1_out, not_1_out, not_2_out);
  not not_3 (not_3_out, A3);
  and and_2 (and_2_out, A3, and_1_out);
  or or_1 (out_5, not_3_out, and_2_out);
endmodule

module BCD_EXCES3 (
  input  in_1,
  input  in_2,
  input  in_3,
  input  in_4,
  output Carry,
  output A3,
  output A2,
  output A1,
  output A0
);

  FourB_ADDER fourb_adder_1 (
    .X3(in_1), .X2(in_2), .Y1(1'b1), .X1(in_3), .Y0(1'b1), .X0(in_4), .Carry(Carry), .S3(A3), .S2(A2),
    .S1(A1), .S0(A0));  // open: Y3, Y2, C
endmodule

module DECODER_2_4 (
  input  E,
  input  A,
  input  B,
  output M0,
  output M1,
  output M2,
  output M3
);

  wire and_1_out, and_2_out, and_3_out, and_4_out, not_1_out, not_2_out;

  not not_1 (not_1_out, A);
  not not_2 (not_2_out, B);
  and and_1 (and_1_out, not_2_out, not_1_out);
  and and_2 (and_2_out, B, not_1_out);
  and and_3 (and_3_out, not_2_out, A);
  and and_4 (and_4_out, B, A);
  and and_5 (M0, and_1_out, E);
  and and_6 (M1, and_2_out, E);
  and and_7 (M2, and_3_out, E);
  and and_8 (M3, and_4_out, E);
endmodule

module DECODER_3_8 (
  input  A,
  input  B,
  input  C,
  output M0,
  output M1,
  output M2,
  output M3,
  output M4,
  output M5,
  output M6,
  output M7
);

  wire not_1_out;

  not not_1 (not_1_out, A);
  DECODER_2_4 decoder_2_4_1 (.E(not_1_out), .A(B), .B(C), .M0(M0), .M1(M1), .M2(M2), .M3(M3));
  DECODER_2_4 decoder_2_4_2 (.E(A), .A(B), .B(C), .M0(M4), .M1(M5), .M2(M6), .M3(M7));
endmodule

module FN (
  input  C,
  input  B,
  input  A
);

  wire decoder_3_8_1_m0, decoder_3_8_1_m1, decoder_3_8_1_m4, decoder_3_8_1_m6;

  DECODER_3_8 decoder_3_8_1 (
    .A(C), .B(B), .C(A), .M0(decoder_3_8_1_m0), .M1(decoder_3_8_1_m1), .M4(decoder_3_8_1_m4),
    .M6(decoder_3_8_1_m6));  // open: M2, M3, M5, M7
  BIG_OR big_or_1 (
    .in_1(decoder_3_8_1_m0), .in_2(decoder_3_8_1_m1), .in_5(decoder_3_8_1_m4), .in_7(decoder_3_8_1_m6));  // open: in_3, in_4, in_6, in_8, out_9
endmodule

module BIG_OR (
  input  in_1,
  input  in_2,
  input  in_3,
  input  in_4,
  input  in_5,
  input  in_6,
  input  in_7,
  input  in_8,
  output out_9
);

  wire or_1_out, or_2_out, or_3_out, or_4_out, or_5_out, or_6_out;

  or or_1 (or_1_out, in_1, in_2);
  or or_2 (or_2_out, or_1_out, in_3);
  or or_3 (or_3_out, or_2_out, in_4);
  or or_4 (or_4_out, or_3_out, in_5);
  or or_5 (or_5_out, or_4_out, in_6);
  or or_6 (or_6_out, or_5_out, in_7);
  or or_7 (out_9, or_6_out, in_8);
endmodule

module ENCODER (
  input  in_1,
  input  in_2,
  input  in_3,
  input  in_4,
  input  in_5,
  input  in_6,
  input  in_7,
  input  in_8,
  output out_9,
  output out_10,
  output out_11
);

  BIG_OR big_or_1 (.in_1(in_2), .in_3(in_4), .in_5(in_6), .in_8(in_8), .out_9(out_9));  // open: in_2, in_4, in_6, in_7
  BIG_OR big_or_2 (.in_1(in_7), .in_2(in_8), .in_3(in_3), .in_4(in_4), .out_9(out_10));  // open: in_5, in_6, in_7, in_8
  BIG_OR big_or_3 (.in_1(in_5), .in_2(in_6), .in_3(in_7), .in_4(in_8), .out_9(out_11));  // open: in_5, in_6, in_7, in_8
endmodule

module MUX_2_1 (
  input  I0,
  input  I1,
  input  S0,
  output out_4
);

  wire and_1_out, and_2_out, not_1_out;

  not not_1 (not_1_out, S0);
  and and_1 (and_1_out, I0, not_1_out);
  and and_2 (and_2_out, I1, S0);
  or or_1 (out_4, and_1_out, and_2_out);
endmodule

module MUX_8_1 (
  input  I0,
  input  I1,
  input  I2,
  input  I3,
  input  I4,
  input  I5,
  input  I6,
  input  I7,
  input  S2,
  input  S1,
  input  S0,
  output out_12
);

  wire and_1_out, and_2_out, and_3_out, and_4_out, and_5_out, and_6_out, and_7_out, and_8_out,
       decoder_3_8_1_m0, decoder_3_8_1_m1, decoder_3_8_1_m2, decoder_3_8_1_m3, decoder_3_8_1_m4,
       decoder_3_8_1_m5, decoder_3_8_1_m6, decoder_3_8_1_m7;

  and and_1 (and_1_out, I0, decoder_3_8_1_m0);
  DECODER_3_8 decoder_3_8_1 (
    .A(S2), .B(S1), .C(S0), .M0(decoder_3_8_1_m0), .M1(decoder_3_8_1_m1), .M2(decoder_3_8_1_m2),
    .M3(decoder_3_8_1_m3), .M4(decoder_3_8_1_m4), .M5(decoder_3_8_1_m5), .M6(decoder_3_8_1_m6),
    .M7(decoder_3_8_1_m7));
  and and_2 (and_2_out, I1, decoder_3_8_1_m1);
  and and_3 (and_3_out, I2, decoder_3_8_1_m2);
  and and_4 (and_4_out, I3, decoder_3_8_1_m3);
  and and_5 (and_5_out, I4, decoder_3_8_1_m4);
  and and_6 (and_6_out, I5, decoder_3_8_1_m5);
  and and_7 (and_7_out, I6, decoder_3_8_1_m6);
  and and_8 (and_8_out, I7, decoder_3_8_1_m7);
  BIG_OR big_or_1 (
    .in_1(and_1_out), .in_2(and_2_out), .in_3(and_3_out), .in_4(and_4_out), .in_5(and_5_out),
    .in_6(and_6_out), .in_7(and_7_out), .in_8(and_8_out), .out_9(out_12));
endmodule

module D_LATCH (
  input  D,
  input  E,
  output Q
);

  wire and_1_out, and_2_out, nor_2_out, not_1_out;

  not not_1 (not_1_out, D);
  and and_1 (and_1_out, not_1_out, E);
  and and_2 (and_2_out, E, D);
  nor nor_1 (Q, and_1_out, nor_2_out);
  nor nor_2 (nor_2_out, Q, and_2_out);
endmodule
