// Logisim project shift_register.circ as structural Verilog: 1 circuit, main circuit main
module main (
  input  D,
  output Q0,
  output Q1,
  output Q2,
  output Q3
);

  wire CLK_out;

  Clock CLK (.out(CLK_out));
  D_Flip_Flop d_ff_1 (.D(D), .clk(CLK_out), .Q(Q0));  // open: Qn, preset, reset
  D_Flip_Flop d_ff_2 (.D(Q0), .clk(CLK_out), .Q(Q1));  // open: Qn, preset, reset
  D_Flip_Flop d_ff_3 (.D(Q1), .clk(CLK_out), .Q(Q2));  // open: Qn, preset, reset
  D_Flip_Flop d_ff_4 (.D(Q2), .clk(CLK_out), .Q(Q3));  // open: Qn, preset, reset
endmodule
